# Fritzing sketch Motor Shield (saved by Fritzing 0.9.2b)
breadboards: 1

parts:
  Part1 = Arduino Motor Shield (Rev3)
  VCC1 = Battery block 9V
  RE1 = Rotary Encoder [package=THT]
  RE2 = Rotary Encoder [package=THT]
  VCC2 = Battery
  M1 = DC Motor
  M2 = DC Motor

nets:
  N1: Part1.D2, RE2.EncoderPinC
  N2: Part1.D7, RE1.EncoderPinC
  N3: Part1.B-, M1.pin_2
  N4: Part1.B+, M1.pin_1
  N5: Part1.A-, M2.pin_2
  N6: Part1.A+, M2.pin_1
  N7: Part1.VMOT, VCC1.+
  N8: Part1.GND, VCC1.-
  N9: RE1.EncoderPinA, RE2.EncoderPinA, VCC2.+
  N10: RE1.EncoderPinB, RE2.EncoderPinB, VCC2.-
