# Fritzing sketch Whole System Diagram (saved by Fritzing 0.9.2b)
breadboards: 1

parts:
  Uno_with_Sensor_Shield = Arduino Uno (Rev3)
  V1 = DC Power [voltage=9]
  Uno_with_Wifi_Shield = Arduino Wireless SD Shield
  Uno_with_Motor_Shield = Arduino Motor Shield (Rev3)
  R1 = Resistor [tolerance=±5% resistance=10k package=THT]
  Color_Sensor = Infrared Proximity Sensor

nets:
  N1: Uno_with_Sensor_Shield.A4/SDA, Uno_with_Sensor_Shield.A5/SCL, Uno_with_Wifi_Shield.A4, Uno_with_Wifi_Shield.A5, Uno_with_Motor_Shield.A4, Uno_with_Motor_Shield.A5, R1.Pin_1
  3V3: Uno_with_Sensor_Shield.3V3, Color_Sensor.Vcc
  GND: Uno_with_Sensor_Shield.GND, Uno_with_Wifi_Shield.GND, Uno_with_Motor_Shield.GND, Color_Sensor.GND
  VIN: Uno_with_Sensor_Shield.VIN, V1.V-, Uno_with_Motor_Shield.VIN
  N2: Uno_with_Sensor_Shield.N/C, Color_Sensor.Vout
  N3: V1.V+, Uno_with_Wifi_Shield.VIN
  N4: Uno_with_Motor_Shield.5V, R1.Pin_0
